// Digital circuit addrCalc.dig as structural Verilog
module addrCalc (
  input  [7:0] Off,
  input  [15:0] Base,
  output [15:0] Addr
);

  Add #(.Bits(16)) add_1 (.a(Base), .b({{8{1'b0}}, Off}), .c_i(1'b0), .s(Addr));  // open: c_o
  // Pins of 1 and 16 bits meet at Addr

  // Notes on the sheet:
  //   Off: Offset to add to the base
  //   Base: Base of the address
  //   Addr: Computed address
endmodule
