// Digital circuit alu.dig as structural Verilog
module alu (
  input  [3:0] Op,
  input  [15:0] TData,
  input  [15:0] AData,
  input  DO,
  input  Clk,
  output [15:0] RData,
  output [3:0] Fl
);

  wire add_1_c_o, and_1_out, and_2_out, and_3_out, and_4_out, and_5_out, comparator_1_eq, not_1_out, Rn,
       sub_1_c_o;
  wire [3:1] multiplexer_3_out;
  wire [14:0] multiplexer_1_out;
  wire [15:0] add_1_s, mul_1_mul, multiplexer_2_out, sub_1_s;
  wire [31:16] mul_1_mul_2;

  Add #(.Bits(16)) add_1 (.a(TData), .b(AData), .c_i(1'b0), .s(add_1_s), .c_o(add_1_c_o));
  Sub #(.Bits(16)) sub_1 (.a(TData), .b(AData), .c_i(1'b0), .s(sub_1_s), .c_o(sub_1_c_o));
  Mul #(.Bits(16)) mul_1 (.a(TData), .b(AData), .mul({mul_1_mul_2, mul_1_mul}));
  Multiplexer #(.Selector_Bits(4), .Bits(16)) multiplexer_1 (
    .sel(Op), .in_0(add_1_s), .in_1(sub_1_s), .in_2(AData), .in_3(TData), .in_4(mul_1_mul),
    .in_5({16{1'b0}}), .in_6({16{1'b0}}), .in_7({16{1'b0}}), .in_8({16{1'b0}}), .in_9({16{1'b0}}),
    .in_10({16{1'b0}}), .in_11({16{1'b0}}), .in_12({16{1'b0}}), .in_13({16{1'b0}}), .in_14({16{1'b0}}),
    .in_15({16{1'b0}}), .out({Rn, multiplexer_1_out}));
  assign RData = DO ? {Rn, multiplexer_1_out} : 16'bz;  // Driver driver_1
  Multiplexer #(.Selector_Bits(4), .Bits(16)) multiplexer_2 (
    .sel(Op), .in_0(add_1_s), .in_1(sub_1_s), .in_2(AData), .in_3(sub_1_s), .in_4(mul_1_mul),
    .in_5({16{1'b0}}), .in_6({16{1'b0}}), .in_7({16{1'b0}}), .in_8({16{1'b0}}), .in_9({16{1'b0}}),
    .in_10({16{1'b0}}), .in_11({16{1'b0}}), .in_12({16{1'b0}}), .in_13({16{1'b0}}), .in_14({16{1'b0}}),
    .in_15({16{1'b0}}), .out(multiplexer_2_out));
  Multiplexer #(.Selector_Bits(4)) multiplexer_3 (
    .sel(Op), .in_0(add_1_c_o), .in_1(sub_1_c_o), .in_2(1'b0), .in_3(sub_1_c_o), .in_4(not_1_out),
    .in_5(1'b0), .in_6(1'b0), .in_7(1'b0), .in_8(1'b0), .in_9(1'b0), .in_10(1'b0), .in_11(1'b0),
    .in_12(1'b0), .in_13(1'b0), .in_14(1'b0), .in_15(1'b0), .out(multiplexer_3_out[2]));
  Comparator #(.Bits(16)) comparator_1 (.a({16{1'b0}}), .b(mul_1_mul_2), .eq(comparator_1_eq));  // open: gt, lt
  not not_1 (not_1_out, comparator_1_eq);
  and and_1 (and_1_out, ~multiplexer_2_out[0], ~multiplexer_2_out[1], ~multiplexer_2_out[2], ~multiplexer_2_out[3], ~multiplexer_2_out[4]);  // And
  and and_2 (and_2_out, ~multiplexer_2_out[5], ~multiplexer_2_out[6], ~multiplexer_2_out[7], ~multiplexer_2_out[8], ~multiplexer_2_out[9]);  // And
  and and_3 (and_3_out, ~multiplexer_2_out[10], ~multiplexer_2_out[11], ~multiplexer_2_out[12], ~multiplexer_2_out[13], ~multiplexer_2_out[14]);  // And
  and and_4 (and_4_out, TData[15], ~AData[15], ~Rn);  // And
  and and_5 (and_5_out, ~TData[15], AData[15], Rn);  // And
  and and_6 (multiplexer_3_out[1], and_1_out, and_2_out, and_3_out, ~multiplexer_2_out[15]);  // And
  or or_1 (multiplexer_3_out[3], and_4_out, and_5_out);
  Register #(.Bits(4)) register_1 (.D({multiplexer_3_out, multiplexer_2_out[15]}), .C(Clk), .en(DO), .Q(Fl));

  // Other names for the same wires on the sheet: An = AData[15]; Tn = TData[15]

  // Notes on the sheet:
  //   Op: Select which operation to perform 
  //   0x0 : Add
  //   0x1 : Subtract
  //   0x2 : Multiply
  //   0x3 : Divide
  //   TData: Data of the target operand
  //   AData: Data of the argument
  //   RData: Result data
  //   Fl: 4 Bit flags: N, Z, C, O
  //   DO: When high, result is visible in RData
  //   Clk: Clock signal
endmodule
