// Digital circuit jumpCalc.dig as structural Verilog
module jumpCalc (
  input  [15:0] PC,
  input  [7:0] Imm,
  input  [15:0] Reg,
  input  JReg,
  input  RRel,
  output [15:0] nPC
);

  wire [15:0] add_1_s, add_2_s, bitextender_1_out, multiplexer_1_out;

  BitExtender bitextender_1 (.in(Imm), .out(bitextender_1_out));
  Add #(.Bits(16)) add_1 (.a(PC), .b(bitextender_1_out), .c_i(1'b0), .s(add_1_s));  // open: c_o
  Add #(.Bits(16)) add_2 (.a(PC), .b(Reg), .c_i(1'b0), .s(add_2_s));  // open: c_o
  Multiplexer #(.Bits(16)) multiplexer_1 (.sel(RRel), .in_0(Reg), .in_1(add_2_s), .out(multiplexer_1_out));
  Multiplexer #(.Bits(16)) multiplexer_2 (.sel(JReg), .in_0(add_1_s), .in_1(multiplexer_1_out), .out(nPC));

  // Notes on the sheet:
  //   JReg: When high, use register computed value
  //   RRel: When high, use regsiter as relative value
  //   nPC: New PC value
endmodule
