// Digital circuit jumpDecider.dig as structural Verilog
module jumpDecider (
  input  Jmp,
  input  [3:0] JT,
  input  [3:0] Fl,
  output DJmp
);

  wire and_1_out, and_2_out, multiplexer_1_out, not_1_out, not_2_out, not_3_out, or_1_out, or_2_out,
       xor_1_out;

  not not_1 (not_1_out, Fl[1]);
  or or_1 (or_1_out, Fl[1], Fl[2]);
  and and_1 (and_1_out, ~Fl[1], ~Fl[2]);  // And
  not not_2 (not_2_out, Fl[2]);
  or or_2 (or_2_out, xor_1_out, Fl[1]);
  xor xor_1 (xor_1_out, Fl[0], Fl[3]);
  and and_2 (and_2_out, ~xor_1_out, ~Fl[1]);  // And
  not not_3 (not_3_out, xor_1_out);
  Multiplexer #(.Selector_Bits(4)) multiplexer_1 (
    .sel(JT), .in_0(Fl[1]), .in_1(not_1_out), .in_2(Fl[3]), .in_3(Fl[0]), .in_4(Fl[2]), .in_5(or_1_out),
    .in_6(and_1_out), .in_7(not_2_out), .in_8(xor_1_out), .in_9(or_2_out), .in_10(and_2_out),
    .in_11(not_3_out), .in_12(1'b0), .in_13(1'b0), .in_14(1'b0), .in_15(1'b1), .out(multiplexer_1_out));
  and and_3 (DJmp, Jmp, multiplexer_1_out);

  // Notes on the sheet:
  //   Jmp: When high, jump
  //   JT: Jump Type
  //   DJmp: High if the given Jump Type should jump
  //   with the given Flags
  //   Equal
  //   Not equal
  //   Signed Overflow
  //   Negative
  //   Unsigned < / Carry
  //   Unsigned <=
  //   Unsigned >
  //   Unsigned >=
  //   Signed <
  //   Signed <=
  //   Signed >
  //   Signed >=
  //   Always
endmodule
