// Digital circuit overwriter.dig as structural Verilog
module overwriter (
  input  [7:0] Data,
  input  Lo,
  input  Hi,
  input  [15:0] Val,
  output [15:0] ValU
);

  assign ValU = Lo ? {Val[15:8], Data} : 16'bz;  // Driver driver_1
  assign ValU = Hi ? {Data, Val[7:0]} : 16'bz;  // Driver driver_2

  // Notes on the sheet:
  //   ValU: The update value
  //   Data: The data to write
  //   Lo: When high, overwrite the low bits with the data
  //   Hi: When high, overwrite the high bits with the data
  //   Val: The value to write over
endmodule
