// Digital circuit pAddr.dig as structural Verilog
module pAddr (
  input  [1:0] A,
  input  En,
  output _0,
  output _1,
  output _2,
  output _3
);

  wire decoder_1_out_0, decoder_1_out_1, decoder_1_out_2, decoder_1_out_3;

  Decoder #(.Selector_Bits(2)) decoder_1 (
    .sel(A), .out_0(decoder_1_out_0), .out_1(decoder_1_out_1), .out_2(decoder_1_out_2),
    .out_3(decoder_1_out_3));
  and and_1 (_0, decoder_1_out_0, En);
  and and_2 (_1, decoder_1_out_1, En);
  and and_3 (_2, decoder_1_out_2, En);
  and and_4 (_3, decoder_1_out_3, En);

  // Notes on the sheet:
  //   A: Peripheral address
  //   En: Enabled when high
endmodule
