// Digital circuit term.dig as structural Verilog
module term (
  input  [15:0] A,
  input  [15:0] Din,
  input  W,
  input  R,
  input  Clk,
  output [15:0] D,
  output [15:0] Fl
);

  Terminal terminal_1 (.D(Din), .C(Clk), .en(W));
  Keyboard keyboard_1 (.C(Clk), .en(R), .D(D), .av(Fl[0]));

  assign Fl[15:1] = {15{1'b0}};

  // Notes on the sheet:
  //   A: Address
  //   Din: Data in
  //   W: When high, write on the clock signal
  //   R: When high, read on the clock signal
  //   D: Data out
  //   Fl: Flags
  //   Clk: Clock signal
endmodule
